// Logisim project alu.circ as structural Verilog: 26 circuits, main circuit alu
module alu (
  input  [31:0] A,
  input  [31:0] B,
  input  [3:0] ALUSel,
  output [31:0] Result
);

  wire [31:0] add_re, and_re, bsel_re, mul_re, mulh_re, mulhu_re, or_re, sll_re, slt_re, sra_re, srl_re,
       sub_re, xor_re;

  Multiplexer #(.enable("false"), .select(4), .width(32)) multiplexer_1 (
    .in0(add_re), .in1(and_re), .in2(or_re), .in3(xor_re), .in4(srl_re), .in5(sra_re), .in6(sll_re),
    .in7(slt_re), .in10(mul_re), .in11(mulhu_re), .in12(sub_re), .in13(bsel_re), .in14(mulh_re),
    .out(Result), .sel(ALUSel));  // open: in8, in9, in15
  Adder #(.width(32)) adder_1 (.a(A), .b(B), .out(add_re));  // open: cin, cout
  assign and_re = A & B;  // AND_Gate and_1, 32 bits wide
  assign or_re = A | B;  // OR_Gate or_1, 32 bits wide
  assign xor_re = A ^ B;  // XOR_Gate xor_1, 32 bits wide
  srl0 srl0_1 (.A(A), .B(B), .out_3(srl_re));
  sra0 sra0_1 (.A(A), .B(B), .out_3(sra_re));
  sll0 sll0_1 (.A(A), .B(B), .out_3(sll_re));
  slt0 slt0_1 (.A(A), .B(B), .out_3(slt_re));
  mul0 mul0_1 (.A(A), .B(B), .out_3(mul_re));
  mulhu mulhu_1 (.A(A), .B(B), .out_3(mulhu_re));
  sub0 sub0_1 (.A(A), .B(B), .out_3(sub_re));
  bsel0 bsel0_1 (.A(A), .B(B), .out_3(bsel_re));
  mulh0 mulh0_1 (.A(A), .B(B), .out_3(mulh_re));

  // Notes on the sheet:
  //   INPUTS to your circuit
  //   DON'T CHANGE THE LOCATIONS OF THE INPUTS AND OUTPUTS!
  //   OUTPUT from your circuit
endmodule

module srl0 (
  input  [31:0] A,
  input  [31:0] B,
  output [31:0] out_3
);

  wire [31:0] A1, A2, A3, A4, A5, A6, A7, A8, A9;

  Multiplexer #(.enable("false"), .width(32)) multiplexer_1 (.in0(A), .in1(A1), .out(A2), .sel(B[0]));
  Multiplexer #(.enable("false"), .width(32)) multiplexer_2 (.in0(A2), .in1(A3), .out(A4), .sel(B[1]));
  srl1 srl1_1 (.in_1(A), .out_2(A1));
  Multiplexer #(.enable("false"), .width(32)) multiplexer_3 (.in0(A4), .in1(A5), .out(A6), .sel(B[2]));
  Multiplexer #(.enable("false"), .width(32)) multiplexer_4 (.in0(A6), .in1(A7), .out(A8), .sel(B[3]));
  srl2 srl2_1 (.in_1(A2), .out_2(A3));
  Multiplexer #(.enable("false"), .width(32)) multiplexer_5 (.in0(A8), .in1(A9), .out(out_3), .sel(B[4]));
  srl4 srl4_1 (.in_1(A4), .out_2(A5));
  srl8 srl8_1 (.in_1(A6), .out_2(A7));
  srl16 srl16_1 (.in_1(A8), .out_2(A9));
endmodule

module srl1 (
  input  [31:0] in_1,
  output [31:0] out_2
);


  assign out_2 = {1'b0, in_1[31:1]};
endmodule

module srl2 (
  input  [31:0] in_1,
  output [31:0] out_2
);


  assign out_2 = {2'b00, in_1[31:2]};
endmodule

module srl4 (
  input  [31:0] in_1,
  output [31:0] out_2
);


  assign out_2 = {4'b0000, in_1[31:4]};
endmodule

module srl8 (
  input  [31:0] in_1,
  output [31:0] out_2
);


  assign out_2 = {{8{1'b0}}, in_1[31:8]};
endmodule

module srl16 (
  input  [31:0] in_1,
  output [31:0] out_2
);


  assign out_2 = {{16{1'b0}}, in_1[31:16]};
endmodule

module or27 (
  input  [26:0] in_1,
  output out_2
);

  wire or_1_out, or_2_out, or_3_out, or_4_out, or_5_out, or_6_out, or_7_out, or_8_out, or_9_out, or_10_out,
       or_11_out, or_12_out, or_13_out, or_14_out, or_15_out, or_16_out, or_17_out, or_18_out, or_19_out,
       or_20_out, or_21_out, or_22_out, or_23_out, or_24_out, or_26_out;

  or or_1 (or_1_out, in_1[0], in_1[1]);
  or or_2 (or_2_out, in_1[2], in_1[3]);
  or or_3 (or_3_out, in_1[4], in_1[5]);
  or or_4 (or_4_out, or_1_out, or_2_out);
  or or_5 (or_5_out, in_1[6], in_1[7]);
  or or_6 (or_6_out, or_4_out, or_7_out);
  or or_7 (or_7_out, or_3_out, or_5_out);
  or or_8 (or_8_out, in_1[8], in_1[9]);
  or or_9 (or_9_out, in_1[10], in_1[11]);
  or or_10 (or_10_out, or_8_out, or_9_out);
  or or_11 (or_11_out, in_1[12], in_1[13]);
  or or_12 (or_12_out, in_1[14], in_1[15]);
  or or_13 (or_13_out, or_10_out, or_14_out);
  or or_14 (or_14_out, or_11_out, or_12_out);
  or or_15 (or_15_out, in_1[16], in_1[17]);
  or or_16 (or_16_out, in_1[18], in_1[19]);
  or or_17 (or_17_out, or_6_out, or_13_out);
  or or_18 (or_18_out, or_15_out, or_16_out);
  or or_19 (or_19_out, in_1[20], in_1[21]);
  or or_20 (or_20_out, in_1[22], in_1[23]);
  or or_21 (or_21_out, or_18_out, or_22_out);
  or or_22 (or_22_out, or_19_out, or_20_out);
  or or_23 (or_23_out, in_1[24], in_1[25]);
  or or_24 (or_24_out, or_23_out, in_1[26]);
  or or_25 (out_2, or_17_out, or_26_out);
  or or_26 (or_26_out, or_21_out, or_24_out);
endmodule

module sra0 (
  input  [31:0] A,
  input  [31:0] B,
  output [31:0] out_3
);

  wire [31:0] A1, A2, A3, A4, A5, A6, A7, A8, A9;

  Multiplexer #(.enable("false"), .width(32)) multiplexer_1 (.in0(A), .in1(A1), .out(A2), .sel(B[0]));
  Multiplexer #(.enable("false"), .width(32)) multiplexer_2 (.in0(A2), .in1(A3), .out(A4), .sel(B[1]));
  sra1 sra1_1 (.in_1(A), .out_2(A1));
  Multiplexer #(.enable("false"), .width(32)) multiplexer_3 (.in0(A4), .in1(A5), .out(A6), .sel(B[2]));
  Multiplexer #(.enable("false"), .width(32)) multiplexer_4 (.in0(A6), .in1(A7), .out(A8), .sel(B[3]));
  sra2 sra2_1 (.in_1(A2), .out_2(A3));
  Multiplexer #(.enable("false"), .width(32)) multiplexer_5 (.in0(A8), .in1(A9), .out(out_3), .sel(B[4]));
  sra4 sra4_1 (.in_1(A4), .out_2(A5));
  sra8 sra8_1 (.in_1(A6), .out_2(A7));
  sra16 sra16_1 (.in_1(A8), .out_2(A9));
endmodule

module sra1 (
  input  [31:0] in_1,
  output [31:0] out_2
);


  assign out_2 = {{2{in_1[31]}}, in_1[30:1]};
endmodule

module sra2 (
  input  [31:0] in_1,
  output [31:0] out_2
);


  assign out_2 = {{3{in_1[31]}}, in_1[30:2]};
endmodule

module sra4 (
  input  [31:0] in_1,
  output [31:0] out_2
);


  assign out_2 = {{5{in_1[31]}}, in_1[30:4]};
endmodule

module sra8 (
  input  [31:0] in_1,
  output [31:0] out_2
);


  assign out_2 = {{9{in_1[31]}}, in_1[30:8]};
endmodule

module sra16 (
  input  [31:0] in_1,
  output [31:0] out_2
);


  assign out_2 = {{17{in_1[31]}}, in_1[30:16]};
endmodule

module sll0 (
  input  [31:0] A,
  input  [31:0] B,
  output [31:0] out_3
);

  wire [31:0] A1, A2, A3, A4, A5, A6, A7, A8, A9;

  Multiplexer #(.enable("false"), .width(32)) multiplexer_1 (.in0(A), .in1(A1), .out(A2), .sel(B[0]));
  Multiplexer #(.enable("false"), .width(32)) multiplexer_2 (.in0(A2), .in1(A3), .out(A4), .sel(B[1]));
  sll1 sll1_1 (.in_1(A), .out_2(A1));
  Multiplexer #(.enable("false"), .width(32)) multiplexer_3 (.in0(A4), .in1(A5), .out(A6), .sel(B[2]));
  Multiplexer #(.enable("false"), .width(32)) multiplexer_4 (.in0(A6), .in1(A7), .out(A8), .sel(B[3]));
  sll2 sll2_1 (.in_1(A2), .out_2(A3));
  Multiplexer #(.enable("false"), .width(32)) multiplexer_5 (.in0(A8), .in1(A9), .out(out_3), .sel(B[4]));
  sll4 sll4_1 (.in_1(A4), .out_2(A5));
  sll8 sll8_1 (.in_1(A6), .out_2(A7));
  sll16 sll16_1 (.in_1(A8), .out_2(A9));

  // Other names for the same wires on the sheet: A10[31:0] = out_3
endmodule

module sll1 (
  input  [31:0] in_1,
  output [31:0] out_2
);


  assign out_2 = {in_1[30:0], 1'b0};
endmodule

module sll2 (
  input  [31:0] in_1,
  output [31:0] out_2
);


  assign out_2 = {in_1[29:0], 2'b00};
endmodule

module sll4 (
  input  [31:0] in_1,
  output [31:0] out_2
);


  assign out_2 = {in_1[27:0], 4'b0000};
endmodule

module sll8 (
  input  [31:0] in_1,
  output [31:0] out_2
);


  assign out_2 = {in_1[23:0], {8{1'b0}}};
endmodule

module sll16 (
  input  [31:0] in_1,
  output [31:0] out_2
);


  assign out_2 = {in_1[15:0], {16{1'b0}}};
endmodule

module slt0 (
  input  [31:0] A,
  input  [31:0] B,
  output [31:0] out_3
);

  wire comparator_1_lt;

  Comparator #(.width(32)) comparator_1 (.a(A), .b(B), .lt(comparator_1_lt));  // open: gt, eq
  Multiplexer #(.enable("false"), .width(32)) multiplexer_1 (
    .in0({32{1'b0}}), .in1(32'h1), .out(out_3), .sel(comparator_1_lt));
endmodule

module mul0 (
  input  [31:0] A,
  input  [31:0] B,
  output [31:0] out_3
);

  Multiplier #(.mode("twosComplement"), .width(32)) multiplier_1 (.a(A), .b(B), .out(out_3));  // open: cin, cout
endmodule

module mulhu (
  input  [31:0] A,
  input  [31:0] B,
  output [31:0] out_3
);

  Multiplier #(.width(32)) multiplier_1 (.a(A), .b(B), .cout(out_3));  // open: out, cin
endmodule

module sub0 (
  input  [31:0] A,
  input  [31:0] B,
  output [31:0] out_3
);

  Subtractor #(.width(32)) subtractor_1 (.a(A), .b(B), .out(out_3));  // open: bin, bout
endmodule

module bsel0 (
  input  [31:0] A,
  input  [31:0] B,
  output [31:0] out_3
);


  assign out_3 = B;
endmodule

module mulh0 (
  input  [31:0] A,
  input  [31:0] B,
  output [31:0] out_3
);

  Multiplier #(.mode("twosComplement"), .width(32)) multiplier_1 (.a(A), .b(B), .cout(out_3));  // open: out, cin
endmodule
