// Logisim project control_logic.circ as structural Verilog: 1 circuit, main circuit control_logic
module control_logic (
  input  [31:0] inst,
  input  BrEq,
  input  BrLt,
  output PCSel,
  output RegWEn,
  output [2:0] ImmSel,
  output BrUn,
  output ASel,
  output BSel,
  output [3:0] ALUSel,
  output MemRW,
  output [1:0] WBSel,
  output CSRSel,
  output CSRWen
);

  wire and_1_out, and_2_out, and_3_out, and_15_out, and_16_out, and_17_out, and_18_out, and_19_out,
       and_20_out, and_21_out, and_22_out, and_23_out, and_24_out, and_25_out, and_26_out, and_48_out,
       and_49_out, and_50_out, and_51_out, and_52_out, and_53_out, comparator_1_eq, comparator_2_eq,
       comparator_3_eq, comparator_4_eq, comparator_5_eq, comparator_6_eq, comparator_7_eq, comparator_8_eq,
       comparator_9_eq, comparator_10_eq, comparator_11_eq, comparator_12_eq, comparator_13_eq,
       comparator_14_eq, comparator_15_eq, comparator_16_eq, comparator_17_eq, comparator_18_eq,
       comparator_19_eq, comparator_20_eq, comparator_21_eq, comparator_22_eq, comparator_23_eq,
       comparator_24_eq, comparator_25_eq, comparator_26_eq, comparator_27_eq, comparator_28_eq,
       comparator_29_eq, comparator_30_eq, comparator_31_eq, comparator_32_eq, comparator_33_eq,
       comparator_34_eq, comparator_35_eq, comparator_36_eq, comparator_37_eq, comparator_38_eq,
       comparator_39_eq, comparator_40_eq, comparator_41_eq, comparator_42_eq, comparator_43_eq,
       comparator_44_eq, comparator_45_eq, comparator_46_eq, comparator_47_eq, comparator_48_eq,
       comparator_49_eq, comparator_50_eq, comparator_51_eq, comparator_52_eq, comparator_53_eq,
       comparator_54_eq, comparator_55_eq, comparator_56_eq, comparator_57_eq, comparator_58_eq,
       comparator_59_eq, comparator_60_eq, comparator_61_eq, comparator_62_eq, comparator_63_eq,
       comparator_64_eq, comparator_65_eq, comparator_66_eq, comparator_67_eq, comparator_68_eq,
       comparator_69_eq, comparator_70_eq, comparator_71_eq, comparator_72_eq, comparator_73_eq,
       comparator_74_eq, comparator_75_eq, comparator_76_eq, comparator_77_eq, comparator_78_eq,
       comparator_79_eq, comparator_83_eq, comparator_84_eq, comparator_85_eq, comparator_86_eq,
       comparator_87_eq, comparator_88_eq, is_add, is_addi, is_and, is_andi, is_auipc, is_beq, is_bge,
       is_bgeu, is_blt, is_bltu, is_bne, is_csrrwi, is_jal, is_jalr, is_lb, is_lh, is_lui, is_lw, is_mul,
       is_mulh, is_mulhu, is_or, is_ori, is_sb, is_sh, is_sll, is_slli, is_slt, is_slti, is_sra, is_srai,
       is_srl, is_srli, is_sub, is_sw, is_xor, is_xori, not_1_out, not_2_out, not_3_out, or_1_out, or_2_out,
       or_3_out, or_4_out, or_5_out, or_6_out, or_8_out, or_9_out, or_11_out;
  wire [1:0] priority_encoder_2_out;
  wire [4:0] bit_extender_2_out, priority_encoder_1_out;
  wire [5:0] coded, high_coded, low_coded;
  wire [15:14] rom_1_data;

  Comparator #(.width(7)) comparator_1 (.a(inst[6:0]), .b(7'b0010011), .eq(comparator_1_eq));  // open: gt, lt
  Comparator #(.width(3)) comparator_2 (.a(inst[14:12]), .b(3'b000), .eq(comparator_2_eq));  // open: gt, lt
  Comparator #(.width(7)) comparator_3 (.a(inst[6:0]), .b(7'b0010011), .eq(comparator_3_eq));  // open: gt, lt
  Comparator #(.width(3)) comparator_4 (.a(inst[14:12]), .b(3'b001), .eq(comparator_4_eq));  // open: gt, lt
  Comparator #(.width(7)) comparator_5 (.a(inst[31:25]), .b({7{1'b0}}), .eq(comparator_5_eq));  // open: gt, lt
  Comparator #(.width(7)) comparator_6 (.a(inst[6:0]), .b(7'b0010011), .eq(comparator_6_eq));  // open: gt, lt
  Comparator #(.width(3)) comparator_7 (.a(inst[14:12]), .b(3'b010), .eq(comparator_7_eq));  // open: gt, lt
  Comparator #(.width(7)) comparator_8 (.a(inst[6:0]), .b(7'b0010011), .eq(comparator_8_eq));  // open: gt, lt
  Comparator #(.width(3)) comparator_9 (.a(inst[14:12]), .b(3'b011), .eq(comparator_9_eq));  // open: gt, lt
  Comparator #(.width(7)) comparator_10 (.a(inst[6:0]), .b(7'b0010011), .eq(comparator_10_eq));  // open: gt, lt
  Comparator #(.width(3)) comparator_11 (.a(inst[14:12]), .b(3'b100), .eq(comparator_11_eq));  // open: gt, lt
  Comparator #(.width(7)) comparator_12 (.a(inst[31:25]), .b({7{1'b0}}), .eq(comparator_12_eq));  // open: gt, lt
  Comparator #(.width(7)) comparator_13 (.a(inst[6:0]), .b(7'b0010011), .eq(comparator_13_eq));  // open: gt, lt
  Comparator #(.width(3)) comparator_14 (.a(inst[14:12]), .b(3'b101), .eq(comparator_14_eq));  // open: gt, lt
  Comparator #(.width(7)) comparator_15 (.a(inst[31:25]), .b(7'b0100000), .eq(comparator_15_eq));  // open: gt, lt
  Comparator #(.width(7)) comparator_16 (.a(inst[6:0]), .b(7'b0010011), .eq(comparator_16_eq));  // open: gt, lt
  Comparator #(.width(3)) comparator_17 (.a(inst[14:12]), .b(3'b110), .eq(comparator_17_eq));  // open: gt, lt
  Comparator #(.width(7)) comparator_18 (.a(inst[6:0]), .b(7'b0010011), .eq(comparator_18_eq));  // open: gt, lt
  Comparator #(.width(3)) comparator_19 (.a(inst[14:12]), .b(3'b111), .eq(comparator_19_eq));  // open: gt, lt
  and and_1 (and_1_out, comparator_4_eq, comparator_5_eq);
  and and_2 (and_2_out, comparator_11_eq, comparator_12_eq);
  and and_3 (and_3_out, comparator_14_eq, comparator_15_eq);
  Comparator #(.width(7)) comparator_20 (.a(inst[6:0]), .b(7'b0000011), .eq(comparator_20_eq));  // open: gt, lt
  Comparator #(.width(3)) comparator_21 (.a(inst[14:12]), .b(3'b000), .eq(comparator_21_eq));  // open: gt, lt
  Comparator #(.width(7)) comparator_22 (.a(inst[6:0]), .b(7'b0000011), .eq(comparator_22_eq));  // open: gt, lt
  Comparator #(.width(3)) comparator_23 (.a(inst[14:12]), .b(3'b001), .eq(comparator_23_eq));  // open: gt, lt
  Comparator #(.width(7)) comparator_24 (.a(inst[6:0]), .b(7'b0000011), .eq(comparator_24_eq));  // open: gt, lt
  Comparator #(.width(3)) comparator_25 (.a(inst[14:12]), .b(3'b010), .eq(comparator_25_eq));  // open: gt, lt
  and and_4 (is_addi, comparator_1_eq, comparator_2_eq);
  and and_5 (is_slli, comparator_3_eq, and_1_out);
  and and_6 (is_slti, comparator_6_eq, comparator_7_eq);
  and and_7 (is_xori, comparator_8_eq, comparator_9_eq);
  and and_8 (is_srli, comparator_10_eq, and_2_out);
  and and_9 (is_srai, comparator_13_eq, and_3_out);
  and and_10 (is_ori, comparator_16_eq, comparator_17_eq);
  and and_11 (is_andi, comparator_18_eq, comparator_19_eq);
  and and_12 (is_lb, comparator_20_eq, comparator_21_eq);
  and and_13 (is_lh, comparator_22_eq, comparator_23_eq);
  and and_14 (is_lw, comparator_24_eq, comparator_25_eq);
  Comparator #(.width(7)) comparator_26 (.a(inst[6:0]), .b(7'b0110011), .eq(comparator_26_eq));  // open: gt, lt
  Comparator #(.width(3)) comparator_27 (.a(inst[14:12]), .b(3'b000), .eq(comparator_27_eq));  // open: gt, lt
  Comparator #(.width(7)) comparator_28 (.a(inst[31:25]), .b({7{1'b0}}), .eq(comparator_28_eq));  // open: gt, lt
  Comparator #(.width(7)) comparator_29 (.a(inst[6:0]), .b(7'b0110011), .eq(comparator_29_eq));  // open: gt, lt
  Comparator #(.width(3)) comparator_30 (.a(inst[14:12]), .b(3'b000), .eq(comparator_30_eq));  // open: gt, lt
  Comparator #(.width(7)) comparator_31 (.a(inst[31:25]), .b(7'b0000001), .eq(comparator_31_eq));  // open: gt, lt
  Comparator #(.width(7)) comparator_32 (.a(inst[6:0]), .b(7'b0110011), .eq(comparator_32_eq));  // open: gt, lt
  Comparator #(.width(3)) comparator_33 (.a(inst[14:12]), .b(3'b000), .eq(comparator_33_eq));  // open: gt, lt
  Comparator #(.width(7)) comparator_34 (.a(inst[31:25]), .b(7'b0100000), .eq(comparator_34_eq));  // open: gt, lt
  Comparator #(.width(7)) comparator_35 (.a(inst[6:0]), .b(7'b0110011), .eq(comparator_35_eq));  // open: gt, lt
  Comparator #(.width(3)) comparator_36 (.a(inst[14:12]), .b(3'b001), .eq(comparator_36_eq));  // open: gt, lt
  Comparator #(.width(7)) comparator_37 (.a(inst[31:25]), .b({7{1'b0}}), .eq(comparator_37_eq));  // open: gt, lt
  Comparator #(.width(7)) comparator_38 (.a(inst[6:0]), .b(7'b0110011), .eq(comparator_38_eq));  // open: gt, lt
  Comparator #(.width(3)) comparator_39 (.a(inst[14:12]), .b(3'b001), .eq(comparator_39_eq));  // open: gt, lt
  Comparator #(.width(7)) comparator_40 (.a(inst[31:25]), .b(7'b0000001), .eq(comparator_40_eq));  // open: gt, lt
  Comparator #(.width(7)) comparator_41 (.a(inst[6:0]), .b(7'b0110011), .eq(comparator_41_eq));  // open: gt, lt
  Comparator #(.width(3)) comparator_42 (.a(inst[14:12]), .b(3'b011), .eq(comparator_42_eq));  // open: gt, lt
  Comparator #(.width(7)) comparator_43 (.a(inst[31:25]), .b(7'b0000001), .eq(comparator_43_eq));  // open: gt, lt
  Comparator #(.width(7)) comparator_44 (.a(inst[6:0]), .b(7'b0110011), .eq(comparator_44_eq));  // open: gt, lt
  Comparator #(.width(3)) comparator_45 (.a(inst[14:12]), .b(3'b010), .eq(comparator_45_eq));  // open: gt, lt
  Comparator #(.width(7)) comparator_46 (.a(inst[31:25]), .b({7{1'b0}}), .eq(comparator_46_eq));  // open: gt, lt
  Comparator #(.width(7)) comparator_47 (.a(inst[6:0]), .b(7'b0110011), .eq(comparator_47_eq));  // open: gt, lt
  Comparator #(.width(3)) comparator_48 (.a(inst[14:12]), .b(3'b100), .eq(comparator_48_eq));  // open: gt, lt
  Comparator #(.width(7)) comparator_49 (.a(inst[31:25]), .b({7{1'b0}}), .eq(comparator_49_eq));  // open: gt, lt
  Comparator #(.width(7)) comparator_50 (.a(inst[6:0]), .b(7'b0110011), .eq(comparator_50_eq));  // open: gt, lt
  Comparator #(.width(3)) comparator_51 (.a(inst[14:12]), .b(3'b101), .eq(comparator_51_eq));  // open: gt, lt
  Comparator #(.width(7)) comparator_52 (.a(inst[31:25]), .b({7{1'b0}}), .eq(comparator_52_eq));  // open: gt, lt
  Comparator #(.width(7)) comparator_53 (.a(inst[6:0]), .b(7'b0110011), .eq(comparator_53_eq));  // open: gt, lt
  Comparator #(.width(3)) comparator_54 (.a(inst[14:12]), .b(3'b101), .eq(comparator_54_eq));  // open: gt, lt
  Comparator #(.width(7)) comparator_55 (.a(inst[31:25]), .b(7'b0100000), .eq(comparator_55_eq));  // open: gt, lt
  Comparator #(.width(7)) comparator_56 (.a(inst[6:0]), .b(7'b0110011), .eq(comparator_56_eq));  // open: gt, lt
  Comparator #(.width(3)) comparator_57 (.a(inst[14:12]), .b(3'b110), .eq(comparator_57_eq));  // open: gt, lt
  Comparator #(.width(7)) comparator_58 (.a(inst[31:25]), .b({7{1'b0}}), .eq(comparator_58_eq));  // open: gt, lt
  Comparator #(.width(7)) comparator_59 (.a(inst[6:0]), .b(7'b0110011), .eq(comparator_59_eq));  // open: gt, lt
  Comparator #(.width(3)) comparator_60 (.a(inst[14:12]), .b(3'b111), .eq(comparator_60_eq));  // open: gt, lt
  Comparator #(.width(7)) comparator_61 (.a(inst[31:25]), .b({7{1'b0}}), .eq(comparator_61_eq));  // open: gt, lt
  and and_15 (and_15_out, comparator_27_eq, comparator_28_eq);
  and and_16 (and_16_out, comparator_30_eq, comparator_31_eq);
  and and_17 (and_17_out, comparator_33_eq, comparator_34_eq);
  and and_18 (and_18_out, comparator_36_eq, comparator_37_eq);
  and and_19 (and_19_out, comparator_39_eq, comparator_40_eq);
  and and_20 (and_20_out, comparator_42_eq, comparator_43_eq);
  and and_21 (and_21_out, comparator_45_eq, comparator_46_eq);
  and and_22 (and_22_out, comparator_48_eq, comparator_49_eq);
  and and_23 (and_23_out, comparator_51_eq, comparator_52_eq);
  and and_24 (and_24_out, comparator_54_eq, comparator_55_eq);
  and and_25 (and_25_out, comparator_57_eq, comparator_58_eq);
  and and_26 (and_26_out, comparator_60_eq, comparator_61_eq);
  and and_27 (is_add, comparator_26_eq, and_15_out);
  and and_28 (is_mul, comparator_29_eq, and_16_out);
  and and_29 (is_sub, comparator_32_eq, and_17_out);
  and and_30 (is_sll, comparator_35_eq, and_18_out);
  and and_31 (is_mulh, comparator_38_eq, and_19_out);
  and and_32 (is_mulhu, comparator_41_eq, and_20_out);
  and and_33 (is_slt, comparator_44_eq, and_21_out);
  and and_34 (is_xor, comparator_47_eq, and_22_out);
  and and_35 (is_srl, comparator_50_eq, and_23_out);
  and and_36 (is_sra, comparator_53_eq, and_24_out);
  and and_37 (is_or, comparator_56_eq, and_25_out);
  and and_38 (is_and, comparator_59_eq, and_26_out);
  Comparator #(.width(7)) comparator_62 (.a(inst[6:0]), .b(7'b1100011), .eq(comparator_62_eq));  // open: gt, lt
  Comparator #(.width(3)) comparator_63 (.a(inst[14:12]), .b(3'b000), .eq(comparator_63_eq));  // open: gt, lt
  Comparator #(.width(7)) comparator_64 (.a(inst[6:0]), .b(7'b1100011), .eq(comparator_64_eq));  // open: gt, lt
  Comparator #(.width(3)) comparator_65 (.a(inst[14:12]), .b(3'b001), .eq(comparator_65_eq));  // open: gt, lt
  Comparator #(.width(7)) comparator_66 (.a(inst[6:0]), .b(7'b1100011), .eq(comparator_66_eq));  // open: gt, lt
  Comparator #(.width(3)) comparator_67 (.a(inst[14:12]), .b(3'b100), .eq(comparator_67_eq));  // open: gt, lt
  Comparator #(.width(7)) comparator_68 (.a(inst[6:0]), .b(7'b1100011), .eq(comparator_68_eq));  // open: gt, lt
  Comparator #(.width(3)) comparator_69 (.a(inst[14:12]), .b(3'b101), .eq(comparator_69_eq));  // open: gt, lt
  Comparator #(.width(7)) comparator_70 (.a(inst[6:0]), .b(7'b1100011), .eq(comparator_70_eq));  // open: gt, lt
  Comparator #(.width(3)) comparator_71 (.a(inst[14:12]), .b(3'b110), .eq(comparator_71_eq));  // open: gt, lt
  Comparator #(.width(7)) comparator_72 (.a(inst[6:0]), .b(7'b1100011), .eq(comparator_72_eq));  // open: gt, lt
  Comparator #(.width(3)) comparator_73 (.a(inst[14:12]), .b(3'b111), .eq(comparator_73_eq));  // open: gt, lt
  and and_39 (is_beq, comparator_62_eq, comparator_63_eq);
  and and_40 (is_bne, comparator_64_eq, comparator_65_eq);
  and and_41 (is_blt, comparator_66_eq, comparator_67_eq);
  and and_42 (is_bge, comparator_68_eq, comparator_69_eq);
  and and_43 (is_bltu, comparator_70_eq, comparator_71_eq);
  and and_44 (is_bgeu, comparator_72_eq, comparator_73_eq);
  Comparator #(.width(7)) comparator_74 (.a(inst[6:0]), .b(7'b0100011), .eq(comparator_74_eq));  // open: gt, lt
  Comparator #(.width(3)) comparator_75 (.a(inst[14:12]), .b(3'b000), .eq(comparator_75_eq));  // open: gt, lt
  Comparator #(.width(7)) comparator_76 (.a(inst[6:0]), .b(7'b0100011), .eq(comparator_76_eq));  // open: gt, lt
  Comparator #(.width(3)) comparator_77 (.a(inst[14:12]), .b(3'b001), .eq(comparator_77_eq));  // open: gt, lt
  Comparator #(.width(7)) comparator_78 (.a(inst[6:0]), .b(7'b0100011), .eq(comparator_78_eq));  // open: gt, lt
  Comparator #(.width(3)) comparator_79 (.a(inst[14:12]), .b(3'b010), .eq(comparator_79_eq));  // open: gt, lt
  ROM #(.addrWidth(6), .dataWidth(16)) rom_1 (
    .addr(coded), .data({rom_1_data, WBSel, MemRW, ALUSel, BSel, ASel, BrUn, ImmSel, RegWEn}));
  not not_1 (not_1_out, BrEq);
  not not_2 (not_2_out, BrLt);
  not not_3 (not_3_out, BrLt);
  and and_45 (is_sb, comparator_74_eq, comparator_75_eq);
  and and_46 (is_sh, comparator_76_eq, comparator_77_eq);
  and and_47 (is_sw, comparator_78_eq, comparator_79_eq);
  and and_48 (and_48_out, BrEq, is_beq);
  and and_49 (and_49_out, not_1_out, is_bne);
  and and_50 (and_50_out, is_blt, BrLt);
  and and_51 (and_51_out, not_2_out, is_bge);
  and and_52 (and_52_out, is_bltu, BrLt);
  and and_53 (and_53_out, not_3_out, is_bgeu);
  or or_1 (or_1_out, and_48_out, and_49_out);
  or or_2 (or_2_out, and_50_out, and_51_out);
  or or_3 (or_3_out, and_52_out, and_53_out);
  or or_4 (or_4_out, is_jalr, is_jal);
  Comparator #(.width(7)) comparator_80 (.a(inst[6:0]), .b(7'b0010111), .eq(is_auipc));  // open: gt, lt
  Comparator #(.width(7)) comparator_81 (.a(inst[6:0]), .b(7'b0110111), .eq(is_lui));  // open: gt, lt
  Comparator #(.width(7)) comparator_82 (.a(inst[6:0]), .b(7'b1101111), .eq(is_jal));  // open: gt, lt
  Comparator #(.width(7)) comparator_83 (.a(inst[6:0]), .b(7'b1100111), .eq(comparator_83_eq));  // open: gt, lt
  Comparator #(.width(3)) comparator_84 (.a(inst[14:12]), .b(3'b000), .eq(comparator_84_eq));  // open: gt, lt
  or or_5 (or_5_out, or_1_out, or_2_out);
  or or_6 (or_6_out, or_3_out, or_4_out);
  and and_54 (is_jalr, comparator_83_eq, comparator_84_eq);
  or or_7 (PCSel, or_5_out, or_6_out);
  Comparator #(.width(7)) comparator_85 (.a(inst[6:0]), .b(7'b1110011), .eq(comparator_85_eq));  // open: gt, lt
  Comparator #(.width(3)) comparator_86 (.a(inst[14:12]), .b(3'b001), .eq(comparator_86_eq));  // open: gt, lt
  Comparator #(.width(7)) comparator_87 (.a(inst[6:0]), .b(7'b1110011), .eq(comparator_87_eq));  // open: gt, lt
  Comparator #(.width(3)) comparator_88 (.a(inst[14:12]), .b(3'b101), .eq(comparator_88_eq));  // open: gt, lt
  and and_55 (CSRSel, comparator_85_eq, comparator_86_eq);
  and and_56 (is_csrrwi, comparator_87_eq, comparator_88_eq);
  or or_8 (or_8_out, is_auipc, is_lui);
  or or_9 (or_9_out, is_jal, is_jalr);
  or or_10 (CSRWen, CSRSel, is_csrrwi);
  Multiplexer #(.enable("false"), .width(6)) multiplexer_1 (
    .in0(low_coded), .in1(high_coded), .out(coded), .sel(or_11_out));
  or or_11 (or_11_out, or_8_out, or_9_out);
  Priority_Encoder #(.select(5)) priority_encoder_1 (
    .in0(is_add), .in1(is_mul), .in2(is_sub), .in3(is_sll), .in4(is_mulh), .in5(is_mulhu), .in6(is_slt),
    .in7(is_xor), .in8(is_srl), .in9(is_sra), .in10(is_or), .in11(is_and), .in12(is_lb), .in13(is_lh),
    .in14(is_lw), .in15(is_addi), .in16(is_slli), .in17(is_slti), .in18(is_xori), .in19(is_srli),
    .in20(is_srai), .in21(is_ori), .in22(is_andi), .in23(is_sb), .in24(is_sh), .in25(is_sw), .in26(is_beq),
    .in27(is_bne), .in28(is_blt), .in29(is_bge), .in30(is_bltu), .in31(is_bgeu), .out(priority_encoder_1_out));  // open: gs, en_out, en_in
  Priority_Encoder #(.select(2)) priority_encoder_2 (
    .in0(is_auipc), .in1(is_lui), .in2(is_jal), .in3(is_jalr), .out(priority_encoder_2_out));  // open: gs, en_out, en_in
  assign low_coded = {{1{1'b0}}, priority_encoder_1_out};  // Bit_Extender bit_extender_1
  assign bit_extender_2_out = {{3{1'b0}}, priority_encoder_2_out};  // Bit_Extender bit_extender_2
  assign high_coded = {{1{1'b1}}, bit_extender_2_out};  // Bit_Extender bit_extender_3

  // Other names for the same wires on the sheet: imm11_0[11:0] = inst[31:20]; funct7[6:0] = inst[31:25];
  //   opcode[6:0] = inst[6:0]; funct3[2:0] = inst[14:12]; is_csrrw = CSRSel

  // Notes on the sheet:
  //   INPUTS to your circuit
  //   DON'T CHANGE THE LOCATIONS OF THE INPUTS AND OUTPUTS!
  //   OUTPUT from your circuit
  //   contents of rom_1 (hex, n*v repeats v):
  //   1001 1501 1601 1301 1701 1581 1381 1181 1201 1281 1101 1081 41 41 41 1041 1341 13c1 11c1 1241 12c1
  //   1141 10c1 842 842 842 4*64 74 74 1067 16c7 2069 2041
endmodule
