// Logisim project cpu.circ as structural Verilog: 1 circuit, main circuit cpu
module cpu (
  input  clk,
  input  [31:0] INSTRUCTION,
  input  [31:0] READ_DATA,
  output [31:0] WRITE_ADDRESS,
  output [31:0] PROGRAM_COUNTER,
  output [31:0] ra,
  output [31:0] sp,
  output [31:0] t0,
  output [31:0] t1,
  output [31:0] t2,
  output [31:0] s0,
  output [31:0] s1,
  output [31:0] a0,
  output [31:0] tohost,
  output [3:0] WRITE_ENABLE,
  output [31:0] WRITE_DATA
);

  wire A_sel, B_eq, B_lt, B_sel, B_un, CSR_sel, CSR_wr_en, ctrl_wr_en, MEM_wr, PC_sel;
  wire [1:0] WB_sel;
  wire [2:0] funct3_0, imm_sel;
  wire [3:0] ALU_sel;
  wire [4:0] imm11_0_0;
  wire [6:0] funct7_0;
  wire [7:0] multiplexer_4_out;
  wire [15:0] multiplexer_5_out;
  wire [19:0] InstFetch;
  wire [31:0] branch_inst, csr_imm, CSR_in, IMM, l_data, lb_re, lh_re, multiplexer_1_out, multiplexer_7_out,
       multiplexer_8_out, PC4, PC_0, PC_4, rs1_data, WB_data;

  Adder #(.width(32)) adder_1 (.a(PROGRAM_COUNTER), .b(32'h4), .out(PC4));  // open: cin, cout
  Register #(.width(32)) PC (.D(multiplexer_1_out), .clk(clk), .Q(PROGRAM_COUNTER));  // open: en, clr
  Multiplexer #(.enable("false"), .width(32)) multiplexer_1 (
    .in0(PC4), .in1(WRITE_ADDRESS), .out(multiplexer_1_out), .sel(PC_sel));
  Register #(.width(32)) register_1 (
    .D(branch_inst), .en(1'b1), .clk(clk),
    .Q({funct7_0, imm11_0_0, InstFetch[19:15], funct3_0, InstFetch[11:0]}));  // open: clr
  Register #(.width(32)) register_2 (.D(PROGRAM_COUNTER), .en(1'b1), .clk(clk), .Q(PC_0));  // open: clr
  Adder #(.width(32)) adder_2 (.a(PC_0), .b(32'h4), .out(PC_4));  // open: cin, cout
  Multiplexer #(.enable("false"), .width(32)) multiplexer_2 (
    .in0(INSTRUCTION), .in1(32'h13), .out(branch_inst), .sel(PC_sel));
  Multiplexer #(.enable("false"), .select(3), .width(32)) multiplexer_3 (
    .in0(lb_re), .in1(lh_re), .in2(READ_DATA), .out(l_data), .sel(funct3_0));  // open: in3, in4, in5, in6, in7
  Multiplexer #(.enable("false"), .select(2), .width(8)) multiplexer_4 (
    .in0(READ_DATA[7:0]), .in1(READ_DATA[15:8]), .in2(READ_DATA[23:16]), .in3(READ_DATA[31:24]),
    .out(multiplexer_4_out), .sel(WRITE_ADDRESS[1:0]));
  imm_gen imm_gen_1 (
    .inst({funct7_0, imm11_0_0, InstFetch[19:15], funct3_0, InstFetch[11:0]}), .ImmSel(imm_sel), .imm(IMM));
  assign lb_re = {{24{multiplexer_4_out[7]}}, multiplexer_4_out};  // Bit_Extender bit_extender_1
  Multiplexer #(.enable("false"), .select(2), .width(16)) multiplexer_5 (
    .in0(READ_DATA[15:0]), .in1(READ_DATA[23:8]), .in2(READ_DATA[31:16]), .out(multiplexer_5_out),
    .sel(WRITE_ADDRESS[1:0]));  // open: in3
  assign lh_re = {{16{multiplexer_5_out[15]}}, multiplexer_5_out};  // Bit_Extender bit_extender_2
  control_logic control_logic_1 (
    .CSRWen(CSR_wr_en), .PCSel(PC_sel), .RegWEn(ctrl_wr_en), .ImmSel(imm_sel), .BrUn(B_un), .ASel(A_sel),
    .BSel(B_sel), .ALUSel(ALU_sel), .MemRW(MEM_wr), .WBSel(WB_sel), .CSRSel(CSR_sel),
    .inst({funct7_0, imm11_0_0, InstFetch[19:15], funct3_0, InstFetch[11:0]}), .BrEq(B_eq), .BrLt(B_lt));
  assign csr_imm = {{27{1'b0}}, InstFetch[19:15]};  // Bit_Extender bit_extender_3
  regfile regfile_1 (
    .rs1(InstFetch[19:15]), .rs2(imm11_0_0), .rd(InstFetch[11:7]), .Write_Data(WB_data), .RegWEn(ctrl_wr_en),
    .clk(clk), .ra(ra), .sp(sp), .t0(t0), .t1(t1), .t2(t2), .s0(s0), .s1(s1), .a0(a0),
    .Read_Data_1(rs1_data), .Read_Data_2(WRITE_DATA));
  Multiplexer #(.enable("false"), .width(32)) multiplexer_6 (
    .in0(csr_imm), .in1(rs1_data), .out(CSR_in), .sel(CSR_sel));
  Multiplexer #(.enable("false"), .width(32)) multiplexer_7 (
    .in0(rs1_data), .in1(PC_0), .out(multiplexer_7_out), .sel(A_sel));
  Multiplexer #(.enable("false"), .width(32)) multiplexer_8 (
    .in0(WRITE_DATA), .in1(IMM), .out(multiplexer_8_out), .sel(B_sel));
  alu alu_1 (.Result(WRITE_ADDRESS), .A(multiplexer_7_out), .B(multiplexer_8_out), .ALUSel(ALU_sel));
  csr csr_1 (.CSR_address({funct7_0, imm11_0_0}), .CSR_din(CSR_in), .CSR_WE(CSR_wr_en), .clk(clk), .tohost(tohost));
  Multiplexer #(.enable("false"), .select(2), .width(32)) multiplexer_9 (
    .in0(l_data), .in1(WRITE_ADDRESS), .in2(PC_4), .out(WB_data), .sel(WB_sel));  // open: in3
  branch_comp branch_comp_1 (.rs1(rs1_data), .rs2(WRITE_DATA), .BrUn(B_un), .BrEq(B_eq), .BrLt(B_lt));
  Multiplexer #(.enable("false"), .select(3), .width(4)) multiplexer_10 (
    .in0(4'b0001), .in1(4'b0011), .in2(4'b1111), .out(WRITE_ENABLE), .sel(funct3_0));  // open: in3, in4, in5, in6, in7

  // Other names for the same wires on the sheet: alu_out[31:0] = WRITE_ADDRESS; imm11_0_0[11:5] = funct7_0;
  //   InstFetch (some bits) = {funct7_0, imm11_0_0, funct3_0}; opcode_0[6:0] = InstFetch[6:0];
  //   rs1_sel[4:0] = InstFetch[19:15]; rd_sel[4:0] = InstFetch[11:7]; rs2_data[31:0] = WRITE_DATA;
  //   rs2_sel[4:0] = imm11_0_0

  // Notes on the sheet:
  //   Output to IMEM
  //   IMEM (do **NOT** move this)
  //   Inputs from IMEM
  //   Inputs/Outputs for testing. Do **NOT** move these.
  //   Outputs To DMEM
  //   DMEM (do **NOT** move this)
  //   Inputs From DMEM
endmodule
