// Logisim project regfile.circ as structural Verilog: 1 circuit, main circuit regfile
module regfile (
  input  [4:0] rs1,
  input  [4:0] rs2,
  input  [4:0] rd,
  input  [31:0] Write_Data,
  input  RegWEn,
  input  clk,
  output [31:0] ra,
  output [31:0] sp,
  output [31:0] t0,
  output [31:0] t1,
  output [31:0] t2,
  output [31:0] s0,
  output [31:0] s1,
  output [31:0] a0,
  output [31:0] Read_Data_1,
  output [31:0] Read_Data_2
);

  wire a0_en, a1_en, a2_en, a3_en, a4_en, a5_en, a6_en, a7_en, gp_en, ra_en, s0_en, s1_en, s2_en, s3_en,
       s4_en, s5_en, s6_en, s7_en, s8_en, s9_en, s10_en, s11_en, sp_en, t0_en, t1_en, t2_en, t3_en, t4_en,
       t5_en, t6_en, tp_en;
  wire [31:0] a0_in, a1, a1_in, a2, a2_in, a3, a3_in, a4, a4_in, a5, a5_in, a6, a6_in, a7, a7_in, gp, gp_in,
       ra_in, s0_in, s1_in, s2, s2_in, s3, s3_in, s4, s4_in, s5, s5_in, s6, s6_in, s7, s7_in, s8, s8_in, s9,
       s9_in, s10, s10_in, s11, s11_in, sp_in, t0_in, t1_in, t2_in, t3, t3_in, t4, t4_in, t5, t5_in, t6,
       t6_in, tp, tp_in, zero_0;

  Register #(.width(32)) zero (.D({32{1'b0}}), .en(1'b0), .clk(clk), .Q(zero_0));  // open: clr
  Register #(.width(32)) s0_fp (.D(s0_in), .en(s0_en), .clk(clk), .Q(s0));  // open: clr
  Register #(.width(32)) a_6 (.D(a6_in), .en(a6_en), .clk(clk), .Q(a6));  // open: clr
  Register #(.width(32)) s_8 (.D(s8_in), .en(s8_en), .clk(clk), .Q(s8));  // open: clr
  Demultiplexer #(.enable("false"), .select(5)) demultiplexer_1 (
    .out1(ra_en), .out2(sp_en), .out3(gp_en), .out4(tp_en), .out5(t0_en), .out6(t1_en), .out7(t2_en),
    .out8(s0_en), .out9(s1_en), .out10(a0_en), .out11(a1_en), .out12(a2_en), .out13(a3_en), .out14(a4_en),
    .out15(a5_en), .out16(a6_en), .out17(a7_en), .out18(s2_en), .out19(s3_en), .out20(s4_en), .out21(s5_en),
    .out22(s6_en), .out23(s7_en), .out24(s8_en), .out25(s9_en), .out26(s10_en), .out27(s11_en),
    .out28(t3_en), .out29(t4_en), .out30(t5_en), .out31(t6_en), .in(RegWEn), .sel(rd));  // open: out0
  Register #(.width(32)) ra_0 (.D(ra_in), .en(ra_en), .clk(clk), .Q(ra));  // open: clr
  Register #(.width(32)) s_1 (.D(s1_in), .en(s1_en), .clk(clk), .Q(s1));  // open: clr
  Register #(.width(32)) a_7 (.D(a7_in), .en(a7_en), .clk(clk), .Q(a7));  // open: clr
  Register #(.width(32)) s_9 (.D(s9_in), .en(s9_en), .clk(clk), .Q(s9));  // open: clr
  Register #(.width(32)) sp_0 (.D(sp_in), .en(sp_en), .clk(clk), .Q(sp));  // open: clr
  Register #(.width(32)) a_0 (.D(a0_in), .en(a0_en), .clk(clk), .Q(a0));  // open: clr
  Register #(.width(32)) s_2 (.D(s2_in), .en(s2_en), .clk(clk), .Q(s2));  // open: clr
  Register #(.width(32)) s_10 (.D(s10_in), .en(s10_en), .clk(clk), .Q(s10));  // open: clr
  Multiplexer #(.enable("false"), .select(5), .width(32)) multiplexer_1 (
    .in0(zero_0), .in1(ra), .in2(sp), .in3(gp), .in4(tp), .in5(t0), .in6(t1), .in7(t2), .in8(s0), .in9(s1),
    .in10(a0), .in11(a1), .in12(a2), .in13(a3), .in14(a4), .in15(a5), .in16(a6), .in17(a7), .in18(s2),
    .in19(s3), .in20(s4), .in21(s5), .in22(s6), .in23(s7), .in24(s8), .in25(s9), .in26(s10), .in27(s11),
    .in28(t3), .in29(t4), .in30(t5), .in31(t6), .out(Read_Data_1), .sel(rs1));
  Register #(.width(32)) gp_0 (.D(gp_in), .en(gp_en), .clk(clk), .Q(gp));  // open: clr
  Register #(.width(32)) a_1 (.D(a1_in), .en(a1_en), .clk(clk), .Q(a1));  // open: clr
  Register #(.width(32)) s_3 (.D(s3_in), .en(s3_en), .clk(clk), .Q(s3));  // open: clr
  Register #(.width(32)) s_11 (.D(s11_in), .en(s11_en), .clk(clk), .Q(s11));  // open: clr
  Register #(.width(32)) tp_0 (.D(tp_in), .en(tp_en), .clk(clk), .Q(tp));  // open: clr
  Register #(.width(32)) a_2 (.D(a2_in), .en(a2_en), .clk(clk), .Q(a2));  // open: clr
  Register #(.width(32)) s_4 (.D(s4_in), .en(s4_en), .clk(clk), .Q(s4));  // open: clr
  Register #(.width(32)) t_3 (.D(t3_in), .en(t3_en), .clk(clk), .Q(t3));  // open: clr
  Demultiplexer #(.enable("false"), .select(5), .width(32)) demultiplexer_2 (
    .out1(ra_in), .out2(sp_in), .out3(gp_in), .out4(tp_in), .out5(t0_in), .out6(t1_in), .out7(t2_in),
    .out8(s0_in), .out9(s1_in), .out10(a0_in), .out11(a1_in), .out12(a2_in), .out13(a3_in), .out14(a4_in),
    .out15(a5_in), .out16(a6_in), .out17(a7_in), .out18(s2_in), .out19(s3_in), .out20(s4_in), .out21(s5_in),
    .out22(s6_in), .out23(s7_in), .out24(s8_in), .out25(s9_in), .out26(s10_in), .out27(s11_in),
    .out28(t3_in), .out29(t4_in), .out30(t5_in), .out31(t6_in), .in(Write_Data), .sel(rd));  // open: out0
  Register #(.width(32)) t_0 (.D(t0_in), .en(t0_en), .clk(clk), .Q(t0));  // open: clr
  Register #(.width(32)) a_3 (.D(a3_in), .en(a3_en), .clk(clk), .Q(a3));  // open: clr
  Register #(.width(32)) s_5 (.D(s5_in), .en(s5_en), .clk(clk), .Q(s5));  // open: clr
  Register #(.width(32)) t_4 (.D(t4_in), .en(t4_en), .clk(clk), .Q(t4));  // open: clr
  Register #(.width(32)) t_1 (.D(t1_in), .en(t1_en), .clk(clk), .Q(t1));  // open: clr
  Register #(.width(32)) a_4 (.D(a4_in), .en(a4_en), .clk(clk), .Q(a4));  // open: clr
  Register #(.width(32)) s_6 (.D(s6_in), .en(s6_en), .clk(clk), .Q(s6));  // open: clr
  Register #(.width(32)) t_5 (.D(t5_in), .en(t5_en), .clk(clk), .Q(t5));  // open: clr
  Multiplexer #(.enable("false"), .select(5), .width(32)) multiplexer_2 (
    .in0(zero_0), .in1(ra), .in2(sp), .in3(gp), .in4(tp), .in5(t0), .in6(t1), .in7(t2), .in8(s0), .in9(s1),
    .in10(a0), .in11(a1), .in12(a2), .in13(a3), .in14(a4), .in15(a5), .in16(a6), .in17(a7), .in18(s2),
    .in19(s3), .in20(s4), .in21(s5), .in22(s6), .in23(s7), .in24(s8), .in25(s9), .in26(s10), .in27(s11),
    .in28(t3), .in29(t4), .in30(t5), .in31(t6), .out(Read_Data_2), .sel(rs2));
  Register #(.width(32)) t_2 (.D(t2_in), .en(t2_en), .clk(clk), .Q(t2));  // open: clr
  Register #(.width(32)) a_5 (.D(a5_in), .en(a5_en), .clk(clk), .Q(a5));  // open: clr
  Register #(.width(32)) s_7 (.D(s7_in), .en(s7_en), .clk(clk), .Q(s7));  // open: clr
  Register #(.width(32)) t_6 (.D(t6_in), .en(t6_en), .clk(clk), .Q(t6));  // open: clr

  // Other names for the same wires on the sheet: read_data1[31:0] = Read_Data_1; read_data2[31:0] = Read_Data_2;
  //   read_reg1[4:0] = rs1; read_reg2[4:0] = rs2; write_en = RegWEn; write_reg[4:0] = rd

  // Notes on the sheet:
  //   INPUTS to your circuit
  //   DON'T CHANGE THE LOCATIONS OF THE INPUTS AND OUTPUTS!
  //   These are DEBUG/TEST outputs from your circuit.
  //   OUTPUTS from your circuit
endmodule
